// Logisim project projetosD.circ as structural Verilog: 3 circuits, main circuit main
module main (
);

  wire clk, igual, muxUla, wbreg, we;
  wire [1:0] Dbreg, OP, PC_sel;
  wire [3:0] opcode;
  wire [7:0] rom_1_data;
  wire [11:0] bancoreg_1_b, imm, multiplexer_1_out, multiplexer_2_out, multiplexer_3_out, multiplexer_4_out,
       PC_1, PC_imm, Ra, ram_1_dout, register_1_q, Sula, undriven;

  Clock clock_1 (.out(clk));
  Multiplexer #(.width(12)) multiplexer_1 (.in0(register_1_q), .in1(PC_imm), .out(multiplexer_1_out), .sel(igual));
  Register #(.width(12)) register_1 (.D(multiplexer_2_out), .en(1'b1), .clk(clk), .Q(register_1_q));  // open: clr
  Multiplexer #(.select(2), .width(12)) multiplexer_2 (
    .in0(PC_1), .in1(PC_imm), .in2(Sula), .in3(multiplexer_1_out), .out(multiplexer_2_out), .sel(PC_sel));
  Adder #(.width(12)) adder_1 (.a(register_1_q), .b(imm), .out(PC_imm));  // open: cin, cout
  Adder #(.width(12)) adder_2 (.a(register_1_q), .b(12'h1), .out(PC_1));  // open: cin, cout
  ROM #(.addrWidth(12), .dataWidth(12)) rom_1 (.addr(register_1_q), .data({opcode, rom_1_data}));
  assign imm = {{8{rom_1_data[3]}}, rom_1_data[3:0]};  // Bit_Extender bit_extender_1
  ROM #(.addrWidth(4), .dataWidth(9)) rom_2 (.addr(opcode), .data({PC_sel, wbreg, muxUla, Dbreg, we, OP}));
  bancoReg bancoreg_1 (
    .D(multiplexer_4_out), .rs1(rom_1_data[2:0]), .W(wbreg), .rd(rom_1_data[2:0]), .rs2(rom_1_data[6:4]),
    .clk(clk), .A(Ra), .B(bancoreg_1_b));
  Multiplexer #(.width(12)) multiplexer_3 (.in0(bancoreg_1_b), .in1(imm), .out(multiplexer_3_out), .sel(muxUla));
  Multiplexer #(.select(2), .width(12)) multiplexer_4 (
    .in0(Sula), .in1(ram_1_dout), .in2(PC_1), .in3(undriven), .out(multiplexer_4_out), .sel(Dbreg));
  Comparator #(.width(12)) comparator_1 (.a(Ra), .b(bancoreg_1_b), .eq(igual));  // open: gt, lt
  ULA ula_1 (.rs1(Ra), .rs2(multiplexer_3_out), .OP(OP), .out_4(Sula));
  RAM #(.addrWidth(12), .dataWidth(12)) ram_1 (
    .addr(bancoreg_1_b), .we(we), .oe(1'b1), .clk(clk), .din(Ra), .dout(ram_1_dout));

  // Notes on the sheet:
  //   contents of rom_2 (hex, n*v repeats v):
  //   40 41 60 42 43 68 24 181 d0 170
endmodule

module bancoReg (
  input  [11:0] D,
  input  [2:0] rs1,
  input  W,
  input  [2:0] rd,
  input  [2:0] rs2,
  input  clk,
  output [11:0] A,
  output [11:0] B
);

  wire demultiplexer_1_out1, demultiplexer_1_out2, demultiplexer_1_out3, demultiplexer_1_out4,
       demultiplexer_1_out5, demultiplexer_1_out6, demultiplexer_1_out7;
  wire [11:0] multiplexer_1_out, multiplexer_2_out, multiplexer_3_out, multiplexer_4_out, multiplexer_5_out,
       multiplexer_6_out, multiplexer_7_out, vr1, vr2, vr3, vr4, vr5, vr6, vr7;

  Demultiplexer #(.select(3)) demultiplexer_1 (
    .out1(demultiplexer_1_out1), .out2(demultiplexer_1_out2), .out3(demultiplexer_1_out3),
    .out4(demultiplexer_1_out4), .out5(demultiplexer_1_out5), .out6(demultiplexer_1_out6),
    .out7(demultiplexer_1_out7), .in(W), .sel(rd));  // open: out0
  Multiplexer #(.width(12)) multiplexer_1 (.in0(vr1), .in1(D), .out(multiplexer_1_out), .sel(demultiplexer_1_out1));
  Multiplexer #(.width(12)) multiplexer_2 (.in0(vr2), .in1(D), .out(multiplexer_2_out), .sel(demultiplexer_1_out2));
  Multiplexer #(.width(12)) multiplexer_3 (.in0(vr3), .in1(D), .out(multiplexer_3_out), .sel(demultiplexer_1_out3));
  Multiplexer #(.width(12)) multiplexer_4 (.in0(vr4), .in1(D), .out(multiplexer_4_out), .sel(demultiplexer_1_out4));
  Multiplexer #(.width(12)) multiplexer_5 (.in0(vr5), .in1(D), .out(multiplexer_5_out), .sel(demultiplexer_1_out5));
  Multiplexer #(.width(12)) multiplexer_6 (.in0(vr6), .in1(D), .out(multiplexer_6_out), .sel(demultiplexer_1_out6));
  Multiplexer #(.width(12)) multiplexer_7 (.in0(vr7), .in1(D), .out(multiplexer_7_out), .sel(demultiplexer_1_out7));
  Register #(.width(12)) r1 (.D(multiplexer_1_out), .clk(clk), .Q(vr1));  // open: en, clr
  Register #(.width(12)) r2 (.D(multiplexer_2_out), .clk(clk), .Q(vr2));  // open: en, clr
  Register #(.width(12)) r3 (.D(multiplexer_3_out), .clk(clk), .Q(vr3));  // open: en, clr
  Register #(.width(12)) r4 (.D(multiplexer_4_out), .clk(clk), .Q(vr4));  // open: en, clr
  Register #(.width(12)) r5 (.D(multiplexer_5_out), .clk(clk), .Q(vr5));  // open: en, clr
  Register #(.width(12)) r6 (.D(multiplexer_6_out), .clk(clk), .Q(vr6));  // open: en, clr
  Register #(.width(12)) r7 (.D(multiplexer_7_out), .clk(clk), .Q(vr7));  // open: en, clr
  Multiplexer #(.select(3), .width(12)) multiplexer_8 (
    .in0({12{1'b0}}), .in1(vr1), .in2(vr2), .in3(vr3), .in4(vr4), .in5(vr5), .in6(vr6), .in7(vr7), .out(A),
    .sel(rs1));
  Multiplexer #(.select(3), .width(12)) multiplexer_9 (
    .in0({12{1'b0}}), .in1(vr1), .in2(vr2), .in3(vr3), .in4(vr4), .in5(vr5), .in6(vr6), .in7(vr7), .out(B),
    .sel(rs2));
endmodule

module ULA (
  input  [11:0] rs1,
  input  [11:0] rs2,
  input  [1:0] OP,
  output [11:0] out_4
);

  wire [11:0] adder_1_out, and_1_out, or_1_out, subtractor_1_out;

  Adder #(.width(12)) adder_1 (.a(rs1), .b(rs2), .out(adder_1_out));  // open: cin, cout
  Subtractor #(.width(12)) subtractor_1 (.a(rs1), .b(rs2), .out(subtractor_1_out));  // open: bin, bout
  assign and_1_out = rs1 & rs2;  // AND_Gate and_1, 12 bits wide
  assign or_1_out = rs1 | rs2;  // OR_Gate or_1, 12 bits wide
  Multiplexer #(.select(2), .width(12)) multiplexer_1 (
    .in0(adder_1_out), .in1(subtractor_1_out), .in2(and_1_out), .in3(or_1_out), .out(out_4), .sel(OP));
endmodule
